# Fritzing sketch brewery-water-controller (saved by Fritzing 0.9.4)
circuit board: 8.46667cm x 5.64444cm
breadboards: 1

parts:
  D1 = Rectifier Diode [part_number=1N4001 package="300 mil [THT]"]
  Q1 = MOSFET-NCHANNEL [package=to220v]
  Solenoid_Connector = JST-03JQ-BT [part_number=JST-JQ-BT package=THT]
  S1 = Pushbutton [package="[THT]"]
  Flow_Meter_Connector = JST-03JQ-BT [part_number=JST-JQ-BT package=THT]
  Part1 = Arduino Uno (Rev3)
  LCD_I2C_Connector = Header 4 [package=screwterminal-3.5mm-4_lock]
  Solenoid_R = Resistor [tolerance=±5% resistance=10k package="0402 [SMD]"]
  Button_R = Resistor [tolerance=±5% resistance=10k package="0805 [SMD]"]
  Flow_R = Resistor [tolerance=±5% resistance=10k package="0805 [SMD]"]

nets:
  N1: D1.cathode, Solenoid_Connector.pin2, Solenoid_Connector.pin1, Part1.VIN
  N2: D1.anode, Q1.D, Solenoid_Connector.pin3
  N3: Q1.G, Part1.D4, Part1.D5_PWM, Solenoid_R.Pin_0
  N4: Q1.S, Flow_Meter_Connector.pin2, Part1.GND, Solenoid_R.Pin_1
  N5: S1.Pin_1, S1.Pin_2, Part1.5V, LCD_I2C_Connector.1, Button_R.Pin_0, Flow_R.Pin_1
  N6: S1.Pin_3, S1.Pin_4, Part1.D3_PWM, Button_R.Pin_1
  N7: Flow_Meter_Connector.pin1, LCD_I2C_Connector.2
  N8: Flow_Meter_Connector.pin3, Part1.D2, Flow_R.Pin_0
  N9: Part1.A4/SDA, LCD_I2C_Connector.3
  N10: Part1.A5/SCL, LCD_I2C_Connector.4
